# Fritzing sketch CAPSTONE_Fritzing (saved by Fritzing 1.0.2b)
breadboards: 1

parts:
  A1 = Particle - Photon2
  OLED_I2C1 = OLED 128x64 I2C Monochrome Display
  Neopixel1 = Adafruit RBG Smart Neopixel [package="DIP (Dual Inline) [THT]"]
  Part1 = KY-003 Hall Magnetic Sensor Module [package="Breakout board"]  # not connected
  X1 = X113647 Stepper Driver Board [part_number=X113647 package=board]  # not connected
  MOTOR1 = 28BYJ-48 Stepper Motor  # not connected
  NEOPIXEL1 = Neopixel Strip -- Black (30/m)  # not connected
  Relay1 = Relay - 6 pins [package="DIP (Dual Inline) [THT]"]  # not connected
  WATER_PUMP1 = water pump/motor  # not connected
  Part2 = InvenSense MPU6050

nets:
  VDD: A1.Pin_2, A1.Pin_31, OLED_I2C1.VDD, Part2.VCC
  GND: A1.Pin_4, A1.Pin_30, OLED_I2C1.GND, Part2.GND
  N1: A1.Pin_17, OLED_I2C1.SCK, Part2.SCL
  N2: A1.Pin_18, OLED_I2C1.SDA, Part2.SDA
  N3: A1.Pin_19, Neopixel1.In

custom parts:
  Particle - Photon2: The Photon 2 is a microcontroller and Wi-Fi networking developed by particle. Features: 802.11a/b/g/n Wi-Fi, 2.4 GHz and 5 GHz Integrated PCB antenna Integrated U.FL connector for external antenna Integrated RF switch BLE 5 using same antenna as Wi-Fi Realtek RTL8721DM MCU ARM Cortex M33 CPU, 200 MHz 2048 KB (2 MB) user application maximum size 3072 KB (3 MB) of RAM available to user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
  KY-003 Hall Magnetic Sensor Module: KEYES KY-003 Arduino Hall Magnetic Sensor Module is a switch that will turn on/off in the presence of a magnetic field.
  X113647 Stepper Driver Board: A common stepper motor driver board based on ULN2003APG darlington array
  28BYJ-48 Stepper Motor: 28BYJ-48 gear-reduction stepper motor (small)
  Neopixel Strip -- Black (30/m): These NeoPixel strips have 30 digitally-addressable pixel LEDs per meter and are very affordable and are only 12.5 mm wide, 10 mm if you remove the strip from the casing.
  Relay - 6 pins: A DIP stand-in part for whatever IC you want. With 6 pins on a 900mil dual inline package (DIP) footprint.
  water pump/motor: WATER PUMP BY ARDUBLOCKTR
